// Logisim project cpu.circ as structural Verilog: 1 circuit, main circuit main
module main (
  input  cin,
  input  [3:0] in_2,
  input  cout,
  input  in_4,
  input  DEFAULT_0N,
  input  clear,
  input  bin,
  input  CF,
  input  ZF,
  input  [7:0] in_10,
  input  bout,
  input  in_12,
  input  in_13,
  input  in_14,
  input  DEFAULT_0N_2,
  output out_16,
  output out_17,
  output out_18,
  output out_19,
  output out_20,
  output out_21,
  output out_22,
  output out_23,
  output out_24,
  output out_25,
  output out_26,
  output out_27,
  output out_28,
  output out_29,
  output out_30,
  output out_31
);

  wire clock_1_out, controlled_buffer_1_out, not_1_out, not_2_out, undriven_3;
  wire [2:0] counter_1_q;
  wire [3:0] controlled_buffer_22_out, counter_2_q, multiplexer_1_out, register_5_q;
  wire [7:0] adder_1_out, multiplexer_2_out, register_1_q, register_2_q, register_3_q, rom_1_data,
       rom_2_data, subtractor_1_out;
  wire [10:9] undriven, undriven_2;

  not not_1 (not_1_out, controlled_buffer_1_out);
  Counter #(.width(3), .max('h7)) counter_1 (
    .count(in_13), .Q(counter_1_q), .clk(not_1_out), .clr(in_14));  // open: load, D, carry
  ROM #(.addrWidth(11)) rom_1 (
    .addr({undriven, ZF, CF, controlled_buffer_22_out, counter_1_q}), .data(rom_1_data));  // open: sel
  ROM #(.addrWidth(11)) rom_2 (
    .addr({undriven_2, ZF, CF, controlled_buffer_22_out, counter_1_q}), .data(rom_2_data));  // open: sel
  not not_2 (not_2_out, rom_1_data[7]);
  Clock clock_1 (.out(clock_1_out));
  assign controlled_buffer_1_out = not_2_out ? clock_1_out : 1'bz;  // Controlled_Buffer controlled_buffer_1
  Register register_1 (
    .D({out_16, out_17, out_18, out_19, out_20, out_21, out_22, out_23}), .en(rom_1_data[1]),
    .Q(register_1_q), .clk(controlled_buffer_1_out), .clr(clear));
  Register register_2 (
    .D({out_16, out_17, out_18, out_19, out_20, out_21, out_22, out_23}), .en(rom_2_data[5]),
    .Q(register_2_q), .clk(controlled_buffer_1_out), .clr(clear));
  Register register_3 (
    .D({out_16, out_17, out_18, out_19, out_20, out_21, out_22, out_23}), .en(rom_1_data[2]),
    .Q(register_3_q), .clk(controlled_buffer_1_out), .clr(clear));
  assign out_23 = rom_1_data[0] ? register_1_q[0] : 1'bz;  // Controlled_Buffer controlled_buffer_2
  assign out_22 = rom_1_data[0] ? register_1_q[1] : 1'bz;  // Controlled_Buffer controlled_buffer_3
  assign out_21 = rom_1_data[0] ? register_1_q[2] : 1'bz;  // Controlled_Buffer controlled_buffer_4
  assign out_20 = rom_1_data[0] ? register_1_q[3] : 1'bz;  // Controlled_Buffer controlled_buffer_5
  assign out_19 = rom_1_data[0] ? register_1_q[4] : 1'bz;  // Controlled_Buffer controlled_buffer_6
  assign out_18 = rom_1_data[0] ? register_1_q[5] : 1'bz;  // Controlled_Buffer controlled_buffer_7
  assign out_17 = rom_1_data[0] ? register_1_q[6] : 1'bz;  // Controlled_Buffer controlled_buffer_8
  assign out_16 = rom_1_data[0] ? register_1_q[7] : 1'bz;  // Controlled_Buffer controlled_buffer_9
  assign out_23 = undriven_3 ? register_2_q[0] : 1'bz;  // Controlled_Buffer controlled_buffer_10
  assign out_22 = undriven_3 ? register_2_q[1] : 1'bz;  // Controlled_Buffer controlled_buffer_11
  assign out_21 = undriven_3 ? register_2_q[2] : 1'bz;  // Controlled_Buffer controlled_buffer_12
  assign out_20 = undriven_3 ? register_2_q[3] : 1'bz;  // Controlled_Buffer controlled_buffer_13
  assign out_19 = undriven_3 ? register_2_q[4] : 1'bz;  // Controlled_Buffer controlled_buffer_14
  assign out_18 = undriven_3 ? register_2_q[5] : 1'bz;  // Controlled_Buffer controlled_buffer_15
  assign out_17 = undriven_3 ? register_2_q[6] : 1'bz;  // Controlled_Buffer controlled_buffer_16
  assign out_16 = undriven_3 ? register_2_q[7] : 1'bz;  // Controlled_Buffer controlled_buffer_17
  assign out_23 = rom_1_data[3] ? register_3_q[0] : 1'bz;  // Controlled_Buffer controlled_buffer_18
  assign out_22 = rom_1_data[3] ? register_3_q[1] : 1'bz;  // Controlled_Buffer controlled_buffer_19
  assign out_21 = rom_1_data[3] ? register_3_q[2] : 1'bz;  // Controlled_Buffer controlled_buffer_20
  assign out_20 = rom_1_data[3] ? register_3_q[3] : 1'bz;  // Controlled_Buffer controlled_buffer_21
  assign controlled_buffer_22_out[0] = rom_1_data[3] ? register_3_q[4] : 1'bz;  // Controlled_Buffer controlled_buffer_22
  assign controlled_buffer_22_out[1] = rom_1_data[3] ? register_3_q[5] : 1'bz;  // Controlled_Buffer controlled_buffer_23
  assign controlled_buffer_22_out[2] = rom_1_data[3] ? register_3_q[6] : 1'bz;  // Controlled_Buffer controlled_buffer_24
  assign controlled_buffer_22_out[3] = rom_1_data[3] ? register_3_q[7] : 1'bz;  // Controlled_Buffer controlled_buffer_25
  Counter #(.width(4), .max('hf)) counter_2 (
    .load(rom_2_data[1]), .D({out_23, out_22, out_21, out_20}), .count(rom_2_data[3]), .Q(counter_2_q),
    .clk(controlled_buffer_1_out), .clr(clear));  // open: carry
  assign {out_20, out_21, out_22, out_23} = rom_2_data[2] ? counter_2_q : 4'bz;  // Controlled_Buffer controlled_buffer_26
  Adder adder_1 (.a(register_1_q), .b(register_2_q), .out(adder_1_out), .cin(cin), .cout(cout));
  Subtractor subtractor_1 (.a(register_1_q), .b(register_2_q), .out(subtractor_1_out), .bin(bin), .bout(bout));
  assign out_23 = rom_2_data[6] ? adder_1_out[0] : 1'bz;  // Controlled_Buffer controlled_buffer_27
  assign out_22 = rom_2_data[6] ? adder_1_out[1] : 1'bz;  // Controlled_Buffer controlled_buffer_28
  assign out_21 = rom_2_data[6] ? adder_1_out[2] : 1'bz;  // Controlled_Buffer controlled_buffer_29
  assign out_20 = rom_2_data[6] ? adder_1_out[3] : 1'bz;  // Controlled_Buffer controlled_buffer_30
  assign out_19 = rom_2_data[6] ? adder_1_out[4] : 1'bz;  // Controlled_Buffer controlled_buffer_31
  assign out_18 = rom_2_data[6] ? adder_1_out[5] : 1'bz;  // Controlled_Buffer controlled_buffer_32
  assign out_17 = rom_2_data[6] ? adder_1_out[6] : 1'bz;  // Controlled_Buffer controlled_buffer_33
  assign out_16 = rom_2_data[6] ? adder_1_out[7] : 1'bz;  // Controlled_Buffer controlled_buffer_34
  assign out_23 = rom_2_data[7] ? subtractor_1_out[0] : 1'bz;  // Controlled_Buffer controlled_buffer_35
  assign out_22 = rom_2_data[7] ? subtractor_1_out[1] : 1'bz;  // Controlled_Buffer controlled_buffer_36
  assign out_21 = rom_2_data[7] ? subtractor_1_out[2] : 1'bz;  // Controlled_Buffer controlled_buffer_37
  assign out_20 = rom_2_data[7] ? subtractor_1_out[3] : 1'bz;  // Controlled_Buffer controlled_buffer_38
  assign out_19 = rom_2_data[7] ? subtractor_1_out[4] : 1'bz;  // Controlled_Buffer controlled_buffer_39
  assign out_18 = rom_2_data[7] ? subtractor_1_out[5] : 1'bz;  // Controlled_Buffer controlled_buffer_40
  assign out_17 = rom_2_data[7] ? subtractor_1_out[6] : 1'bz;  // Controlled_Buffer controlled_buffer_41
  assign out_16 = rom_2_data[7] ? subtractor_1_out[7] : 1'bz;  // Controlled_Buffer controlled_buffer_42
  Multiplexer #(.width(4)) multiplexer_1 (
    .in0(in_2), .in1({out_20, out_21, out_22, out_23}), .out(multiplexer_1_out), .sel(in_4), .en(DEFAULT_0N));
  Register register_4 (
    .D({out_16, out_17, out_18, out_19, out_20, out_21, out_22, out_23}), .en(rom_2_data[4]),
    .Q({out_31, out_30, out_29, out_28, out_27, out_26, out_25, out_24}), .clk(controlled_buffer_1_out),
    .clr(clear));
  Register #(.width(4)) register_5 (
    .D(multiplexer_1_out), .en(rom_1_data[6]), .Q(register_5_q), .clk(controlled_buffer_1_out), .clr(clear));
  Multiplexer #(.width(8)) multiplexer_2 (
    .in0(in_10), .in1({out_16, out_17, out_18, out_19, out_20, out_21, out_22, out_23}),
    .out(multiplexer_2_out), .sel(in_12), .en(DEFAULT_0N_2));
  RAM #(.addrWidth(4), .bus("separate")) ram_1 (
    .addr(register_5_q), .din(multiplexer_2_out),
    .data({out_16, out_17, out_18, out_19, out_20, out_21, out_22, out_23}), .str(rom_1_data[5]),
    .clk(controlled_buffer_1_out), .ld(rom_1_data[4]), .clr(clear));  // open: sel
  // also tied to GND on the sheet: {out_19, out_18, out_17, out_16}

  // Notes on the sheet:
  //   main_clk
  //   contents of rom_1 (hex, n*v repeats v):
  //   40 14 6*0 40 14 48 12 4*0 40 14 48 10 2 0 0 0 40 14 48 10 2 0 0 0 40 14 48 21 4*0 40 14 a 5*0 40 14
  //   8 5*0 40 14 6*0 40 14 6*0 40 14 6*0 40 14 6*0 40 14 6*0 40 14 6*0 40 14 6*0 40 14 1 5*0 40 14 80 5*0
  //   40 14 6*0 40 14 48 12 4*0 40 14 48 10 2 0 0 0 40 14 48 10 2 0 0 0 40 14 48 21 4*0 40 14 a 5*0 40 14
  //   8 5*0 40 14 8 5*0 40 14 6*0 40 14 6*0 40 14 6*0 40 14 6*0 40 14 6*0 40 14 6*0 40 14 1 5*0 40 14 80
  //   5*0 40 14 6*0 40 14 48 12 4*0 40 14 48 10 2 0 0 0 40 14 48 10 2 0 0 0 40 14 48 21 4*0 40 14 a 5*0 40
  //   14 8 5*0 40 14 6*0 40 14 8 5*0 40 14 6*0 40 14 6*0 40 14 6*0 40 14 6*0 40 14 6*0 40 14 1 5*0 40 14
  //   80 5*0 40 14 6*0 40 14 48 12 4*0 40 14 48 10 2 0 0 0 40 14 48 10 2 0 0 0 40 14 48 21 4*0 40 14 a 5*0
  //   40 14 8 5*0 40 14 8 5*0 40 14 8 5*0 40 14 6*0 40 14 6*0 40 14 6*0 40 14 6*0 40 14 6*0 40 14 1 5*0 40
  //   14 80
  //   contents of rom_2 (hex, n*v repeats v):
  //   40 14 6*0 40 14 48 12 4*0 40 14 48 10 2 0 0 0 40 14 48 10 2 0 0 0 40 14 48 21 4*0 40 14 a 5*0 40 14
  //   8 5*0 40 14 6*0 40 14 6*0 40 14 6*0 40 14 6*0 40 14 6*0 40 14 6*0 40 14 6*0 40 14 1 5*0 40 14 80 5*0
  //   40 14 6*0 40 14 48 12 4*0 40 14 48 10 2 0 0 0 40 14 48 10 2 0 0 0 40 14 48 21 4*0 40 14 a 5*0 40 14
  //   8 5*0 40 14 8 5*0 40 14 6*0 40 14 6*0 40 14 6*0 40 14 6*0 40 14 6*0 40 14 6*0 40 14 1 5*0 40 14 80
  //   5*0 40 14 6*0 40 14 48 12 4*0 40 14 48 10 2 0 0 0 40 14 48 10 2 0 0 0 40 14 48 21 4*0 40 14 a 5*0 40
  //   14 8 5*0 40 14 6*0 40 14 8 5*0 40 14 6*0 40 14 6*0 40 14 6*0 40 14 6*0 40 14 6*0 40 14 1 5*0 40 14
  //   80 5*0 40 14 6*0 40 14 48 12 4*0 40 14 48 10 2 0 0 0 40 14 48 10 2 0 0 0 40 14 48 21 4*0 40 14 a 5*0
  //   40 14 8 5*0 40 14 8 5*0 40 14 8 5*0 40 14 6*0 40 14 6*0 40 14 6*0 40 14 6*0 40 14 6*0 40 14 1 5*0 40
  //   14 80
  //   MEM
  //   AD
  //   RAM INPUT en SIGNAL
  //   clk_HLT
  //   AD en
  //   jump
  //   count rnable
  //   output enable
  //   clear
  //   input enable 
  //   clear
  //   en
  //   clear
  //   en_out
  //   sum out
  //   sub out
  //   clear
  //   en
  //   clear
  //   OUT
  //   clear
  //   en
  //   clear
  //   en_out
  //   clk
  //   clk
  //   clk
  //   clk
  //   IR
  //   RA
  //   en_out
  //   PC
  //   address chosing mode
  //   0 = programming mode
  //   RB
  //   AD
  //   clk
  //   OUTPUT
  //   Manual programming
  //   0 = programming mode
  //   MEM
endmodule
